// Logisim project hamming_basic_1.circ as structural Verilog: 1 circuit, main circuit main
module main (
);

  wire dipswitch_1_p1, dipswitch_1_p2, dipswitch_1_p3, dipswitch_1_p4, xor_1_out, xor_2_out, xor_3_out,
       xor_4_out, xor_5_out, xor_6_out;

  // DipSwitch #(.number(4)) dipswitch_1: pin names not known; wires that end beside it: dipswitch_1_p1, dipswitch_1_p2, dipswitch_1_p3, dipswitch_1_p4
  xor xor_1 (xor_1_out, dipswitch_1_p3, dipswitch_1_p2);
  xor xor_2 (xor_2_out, dipswitch_1_p1, dipswitch_1_p2);
  xor xor_3 (xor_3_out, dipswitch_1_p1, dipswitch_1_p3);
  xor xor_4 (xor_4_out, xor_1_out, dipswitch_1_p4);
  xor xor_5 (xor_5_out, xor_2_out, dipswitch_1_p4);
  xor xor_6 (xor_6_out, xor_3_out, dipswitch_1_p4);
  LED led_1 (.in(xor_4_out));
  LED led_2 (.in(xor_5_out));
  LED led_3 (.in(xor_6_out));
endmodule
